// Logisim project LC-2200-16.circ as structural Verilog: 2 circuits, main circuit main
module main (
);

  wire comparator_1_eq, DrALU, DrMEM, DrOFF, DrPC, DrREG, LdA, LdB, LdIR, LdMAR, LdPC, LdZ, timer, WrMEM,
       WrREG;
  wire [1:0] CTRLCD, func;
  wire [2:0] opcode;
  wire [3:0] oregano, RX, RY;
  wire [3:1] RZ;
  wire [15:0] A_q, ALU_output, B_q, bit_extender_1_out, controlled_buffer_1_out, MAR_q, PC_q, ram_1_data,
       ram_2_data;

  Clock clock_1 (.out(timer));
  Register #(.width(16)) PC (.D(controlled_buffer_1_out), .en(LdPC), .Q(PC_q), .clk(timer));  // open: clr
  assign controlled_buffer_1_out = DrPC ? PC_q : 16'bz;  // Controlled_Buffer controlled_buffer_1
  Register #(.width(16)) A (.D(controlled_buffer_1_out), .en(LdA), .Q(A_q), .clk(timer));  // open: clr
  Comparator #(.width(16)) comparator_1 (
    .a(controlled_buffer_1_out), .b({16{1'b0}}), .eq(comparator_1_eq));  // open: gt, lt
  Register #(.width(16)) B (.D(controlled_buffer_1_out), .en(LdB), .Q(B_q), .clk(timer));  // open: clr
  ALU ALU (.func(func), .A(A_q), .B(B_q), .Output(ALU_output));
  assign controlled_buffer_1_out = DrALU ? ALU_output : 16'bz;  // Controlled_Buffer controlled_buffer_2
  Register #(.width(1)) register_1 (.D(comparator_1_eq), .en(LdZ));  // open: Q, clk, clr
  RAM #(.addrWidth(4), .dataWidth(16), .bus("separate")) ram_1 (
    .addr(oregano), .din(controlled_buffer_1_out), .data(ram_1_data), .str(WrREG), .clk(timer), .ld(1'b1));  // open: sel, clr
  assign controlled_buffer_1_out = DrREG ? ram_1_data : 16'bz;  // Controlled_Buffer controlled_buffer_3
  Register #(.width(16)) MAR (.D(controlled_buffer_1_out), .en(LdMAR), .Q(MAR_q), .clk(timer));  // open: clr
  Register #(.width(16)) IR (
    .D(controlled_buffer_1_out), .en(LdIR), .Q({opcode, RX, RY, RZ, CTRLCD}), .clk(timer));  // open: clr
  RAM #(.addrWidth(16), .dataWidth(16), .bus("separate")) ram_2 (
    .addr(MAR_q), .din(controlled_buffer_1_out), .data(ram_2_data), .str(WrMEM), .clk(timer), .ld(1'b1));  // open: sel, clr
  assign controlled_buffer_1_out = DrMEM ? ram_2_data : 16'bz;  // Controlled_Buffer controlled_buffer_4
  assign bit_extender_1_out = {{11{1'b0}}, {RZ, CTRLCD}};  // Bit_Extender bit_extender_1
  assign controlled_buffer_1_out = DrOFF ? bit_extender_1_out : 16'bz;  // Controlled_Buffer controlled_buffer_5

  // Other names for the same wires on the sheet: RZ[0] = CTRLCD[1]
endmodule

module ALU (
  input  [15:0] A,
  input  [15:0] B,
  input  [1:0] func,
  output [15:0] Output
);

  wire [15:0] adder_1_out, adder_2_out, nand_1_out, subtractor_1_out;

  Subtractor #(.width(16)) subtractor_1 (.a(A), .b(B), .out(subtractor_1_out));  // open: bin, bout
  assign nand_1_out = ~(A & B);  // NAND_Gate nand_1, 16 bits wide
  Adder #(.width(16)) adder_1 (.a(A), .b(B), .out(adder_1_out));  // open: cin, cout
  Adder #(.width(16)) adder_2 (.a(16'h1), .b(A), .out(adder_2_out));  // open: cin, cout
  Multiplexer #(.select(2), .width(16)) multiplexer_1 (
    .in0(adder_1_out), .in1(nand_1_out), .in2(subtractor_1_out), .in3(adder_2_out), .out(Output), .sel(func),
    .en(1'b1));
endmodule
